// Logisim project ETFStudent.circ as structural Verilog: 11 circuits, main circuit KMADR
module REG32_LD (
  input  [31:0] I15__0,
  input  LD,
  input  mr,
  input  CLK,
  output [31:0] A15__0
);

  REG16_LD reg16_ld_1 (.I15__0(I15__0[31:16]), .LD(LD), .CLK(CLK), .A15__0(A15__0[31:16]), .mr(mr));
  REG16_LD reg16_ld_2 (.I15__0(I15__0[15:0]), .LD(LD), .CLK(CLK), .A15__0(A15__0[15:0]), .mr(mr));

  // Notes on the sheet:
  //   __
endmodule

module KMADR (
  input  immed,
  input  memdir,
  input  regdir,
  input  regind,
  input  brpom,
  input  xrpom,
  input  bxpom,
  output [3:0] Adr3__0
);

  assign Adr3__0 = immed ? 4'b0010 : 4'bz;  // Controlled_Buffer controlled_buffer_1
  assign Adr3__0 = memdir ? 4'b0011 : 4'bz;  // Controlled_Buffer controlled_buffer_2
  assign Adr3__0 = regdir ? 4'b0100 : 4'bz;  // Controlled_Buffer controlled_buffer_3
  assign Adr3__0 = regind ? 4'b0101 : 4'bz;  // Controlled_Buffer controlled_buffer_4
  assign Adr3__0 = brpom ? 4'b0110 : 4'bz;  // Controlled_Buffer controlled_buffer_5
  assign Adr3__0 = bxpom ? 4'b0110 : 4'bz;  // Controlled_Buffer controlled_buffer_6
  assign Adr3__0 = xrpom ? 4'b0110 : 4'bz;  // Controlled_Buffer controlled_buffer_7
endmodule

module KMOPR (
  input  HALT,
  input  RTS,
  input  RTI,
  input  STBR0,
  input  STXR0,
  input  STBR1,
  input  STXR1,
  input  STRCPY,
  input  STAR,
  input  JNEQ,
  input  JLSSU,
  input  JLSS,
  input  JMP,
  input  LD,
  input  ST,
  input  AND,
  input  ADD,
  input  CMP,
  input  JSR,
  input  CLR,
  output [5:0] Adr5__0
);

  assign Adr5__0 = HALT ? 6'b000010 : 6'bz;  // Controlled_Buffer controlled_buffer_1
  assign Adr5__0 = RTS ? 6'b000011 : 6'bz;  // Controlled_Buffer controlled_buffer_2
  assign Adr5__0 = RTI ? 6'b000111 : 6'bz;  // Controlled_Buffer controlled_buffer_3
  assign Adr5__0 = STBR0 ? 6'b001101 : 6'bz;  // Controlled_Buffer controlled_buffer_4
  assign Adr5__0 = STXR0 ? 6'b001101 : 6'bz;  // Controlled_Buffer controlled_buffer_5
  assign Adr5__0 = STBR1 ? 6'b001101 : 6'bz;  // Controlled_Buffer controlled_buffer_6
  assign Adr5__0 = STXR1 ? 6'b001101 : 6'bz;  // Controlled_Buffer controlled_buffer_7
  assign Adr5__0 = STRCPY ? 6'b001110 : 6'bz;  // Controlled_Buffer controlled_buffer_8
  assign Adr5__0 = STAR ? 6'b001101 : 6'bz;  // Controlled_Buffer controlled_buffer_9
  assign Adr5__0 = JNEQ ? 6'b010101 : 6'bz;  // Controlled_Buffer controlled_buffer_10
  assign Adr5__0 = JLSSU ? 6'b010101 : 6'bz;  // Controlled_Buffer controlled_buffer_11
  assign Adr5__0 = JLSS ? 6'b010101 : 6'bz;  // Controlled_Buffer controlled_buffer_12
  assign Adr5__0 = JMP ? 6'b010110 : 6'bz;  // Controlled_Buffer controlled_buffer_13
  assign Adr5__0 = LD ? 6'b010111 : 6'bz;  // Controlled_Buffer controlled_buffer_14
  assign Adr5__0 = ST ? 6'b011001 : 6'bz;  // Controlled_Buffer controlled_buffer_15
  assign Adr5__0 = AND ? 6'b011110 : 6'bz;  // Controlled_Buffer controlled_buffer_16
  assign Adr5__0 = ADD ? 6'b011111 : 6'bz;  // Controlled_Buffer controlled_buffer_17
  assign Adr5__0 = CMP ? 6'b100000 : 6'bz;  // Controlled_Buffer controlled_buffer_18
  assign Adr5__0 = JSR ? 6'b100001 : 6'bz;  // Controlled_Buffer controlled_buffer_19
  assign Adr5__0 = CLR ? 6'b100100 : 6'bz;  // Controlled_Buffer controlled_buffer_20
endmodule

module REG6_INC_LD (
  input  [5:0] I5__0,
  input  LD,
  input  INC,
  input  mr,
  input  CLK,
  output [5:0] A5__0
);

  wire reg2m_inc_ld_2_cout, reg2m_inc_ld_3_cout;

  REG2m_INC_LD reg2m_inc_ld_1 (
    .I1__0(I5__0[5:4]), .LD(LD), .Cin(reg2m_inc_ld_2_cout), .INC(INC), .CLK(CLK), .A1__0(A5__0[5:4]), .mr(mr));  // open: Cout
  REG2m_INC_LD reg2m_inc_ld_2 (
    .I1__0(I5__0[3:2]), .LD(LD), .Cin(reg2m_inc_ld_3_cout), .INC(INC), .CLK(CLK), .Cout(reg2m_inc_ld_2_cout),
    .A1__0(A5__0[3:2]), .mr(mr));
  REG2m_INC_LD reg2m_inc_ld_3 (
    .I1__0(I5__0[1:0]), .LD(LD), .Cin(INC), .INC(INC), .CLK(CLK), .Cout(reg2m_inc_ld_3_cout),
    .A1__0(A5__0[1:0]), .mr(mr));

  // Notes on the sheet:
  //   __
endmodule

module MEM_64Kx16 (
  input  WR_RD,
  input  [15:0] A15__0,
  input  [15:0] DIN,
  input  CS,
  input  CLK,
  output [15:0] DOUT
);

  wire not_1_out;

  RAM #(.addrWidth(16), .dataWidth(16), .bus("separate")) ram_1 (
    .addr(A15__0), .din(DIN), .data(DOUT), .str(WR_RD), .sel(CS), .clk(CLK), .ld(not_1_out), .clr(1'b0));
  not not_1 (not_1_out, WR_RD);

  // Notes on the sheet:
  //   __
endmodule

module ROM_16x17 (
  input  [3:0] A3__0,
  input  CS,
  output [16:0] DOUT
);

  ROM #(.addrWidth(4), .dataWidth(17)) rom_1 (.addr(A3__0), .data(DOUT), .sel(CS));

  // Notes on the sheet:
  //   contents of rom_1 (hex, n*v repeats v):
  //   400 3 460c 10 1a800 16a00 3 e60c 20 1ac00 1ae00 1000 2c0 1000 340
endmodule

module DRF2x32 (
  input  [15:0] DI15__0,
  input  [3:0] A3__0,
  input  WR,
  input  CLK,
  output [31:0] DO31__0
);

  wire and_1_out, and_2_out, and_3_out, and_4_out, and_5_out, and_6_out, CS0, CS1, CS2, CS3, CS4, CS5, CS6,
       CS7, CS8, CS9, or_1_out, or_2_out, or_3_out, or_4_out;
  wire [15:0] mp2_16b_1_out_5, mp2_16b_2_out_5, reg16m_inc_ld_1_a15__0, reg16m_inc_ld_2_a15__0,
       reg16m_inc_ld_3_a15__0, reg16m_inc_ld_4_a15__0, reg16m_inc_ld_5_a15__0, reg16m_inc_ld_6_a15__0;

  DC4_16 dc4_16_1 (
    .En(1'b1), .X3__0(A3__0), .D0(CS0), .D1(CS1), .D2(CS2), .D3(CS3), .D4(CS4), .D5(CS5), .D6(CS6), .D7(CS7),
    .D8(CS8), .D9(CS9));  // open: D10, D11, D12, D13, D14, D15
  and and_1 (and_1_out, or_1_out, WR);
  REG16m_INC_LD reg16m_inc_ld_1 (
    .I15__0(DI15__0), .LD(and_1_out), .CLK(CLK), .A15__0(reg16m_inc_ld_1_a15__0));  // open: Cin, INC, mr, Cout
  assign DO31__0[15:0] = CS0 ? reg16m_inc_ld_1_a15__0 : 16'bz;  // Controlled_Buffer controlled_buffer_1
  MP2_16b mp2_16b_1 (.En(1'b1), .in_2(DI15__0), .in_3(reg16m_inc_ld_1_a15__0), .S0(CS8), .out_5(mp2_16b_1_out_5));
  REG16m_INC_LD reg16m_inc_ld_2 (
    .I15__0(mp2_16b_1_out_5), .LD(and_2_out), .INC(CS9), .CLK(CLK), .A15__0(reg16m_inc_ld_2_a15__0));  // open: Cin, mr, Cout
  assign DO31__0[31:16] = CS0 ? reg16m_inc_ld_2_a15__0 : 16'bz;  // Controlled_Buffer controlled_buffer_2
  REG16m_INC_LD reg16m_inc_ld_3 (
    .I15__0(DI15__0), .LD(and_3_out), .CLK(CLK), .A15__0(reg16m_inc_ld_3_a15__0));  // open: Cin, INC, mr, Cout
  assign DO31__0[15:0] = CS2 ? reg16m_inc_ld_3_a15__0 : 16'bz;  // Controlled_Buffer controlled_buffer_3
  or or_1 (or_1_out, CS0, CS4);
  and and_2 (and_2_out, or_2_out, WR);
  and and_3 (and_3_out, CS2, WR);
  or or_2 (or_2_out, CS0, CS6, CS8);
  REG16m_INC_LD reg16m_inc_ld_4 (
    .I15__0(DI15__0), .LD(and_4_out), .CLK(CLK), .A15__0(reg16m_inc_ld_4_a15__0));  // open: Cin, INC, mr, Cout
  assign DO31__0[15:0] = CS1 ? reg16m_inc_ld_4_a15__0 : 16'bz;  // Controlled_Buffer controlled_buffer_4
  MP2_16b mp2_16b_2 (.En(1'b1), .in_2(DI15__0), .in_3(reg16m_inc_ld_4_a15__0), .S0(CS8), .out_5(mp2_16b_2_out_5));
  REG16m_INC_LD reg16m_inc_ld_5 (
    .I15__0(mp2_16b_2_out_5), .LD(and_5_out), .INC(CS9), .CLK(CLK), .A15__0(reg16m_inc_ld_5_a15__0));  // open: Cin, mr, Cout
  assign DO31__0[31:16] = CS1 ? reg16m_inc_ld_5_a15__0 : 16'bz;  // Controlled_Buffer controlled_buffer_5
  REG16m_INC_LD reg16m_inc_ld_6 (
    .I15__0(DI15__0), .LD(and_6_out), .CLK(CLK), .A15__0(reg16m_inc_ld_6_a15__0));  // open: Cin, INC, mr, Cout
  assign DO31__0[15:0] = CS3 ? reg16m_inc_ld_6_a15__0 : 16'bz;  // Controlled_Buffer controlled_buffer_6
  or or_3 (or_3_out, CS1, CS5);
  and and_4 (and_4_out, or_3_out, WR);
  and and_5 (and_5_out, or_4_out, WR);
  and and_6 (and_6_out, CS3, WR);
  or or_4 (or_4_out, CS1, CS7, CS8);

  // Other names for the same wires on the sheet: outREG1[15:0] = DO31__0[15:0]; outREG2[15:0] = DO31__0[31:16];
  //   inREG[15:0] = DI15__0

  // Notes on the sheet:
  //   R[0]
  //   R[1]
  //   DR
  //   AR
  //   BR[0]
  //   BR[1]
  //   XR[0]
  //   XR[1]
  //   setpointers
  //   incpointers
  //   BR0
  //   XR0
  //   DR
  //   BR1
  //   AR
  //   XR1
endmodule

module ALU16_ADD_SUBB_AND (
  input  Cin,
  input  [15:0] A,
  input  [15:0] B,
  input  add,
  input  sub,
  input  \and ,
  output [15:0] F,
  output Cout
);

  wire adder_1_cout, subtractor_1_bout;
  wire [15:0] adder_1_out, and_1_out, subtractor_1_out;

  Adder #(.width(16)) adder_1 (.a(A), .b(B), .out(adder_1_out), .cin(Cin), .cout(adder_1_cout));
  Subtractor #(.width(16)) subtractor_1 (.a(A), .b(B), .out(subtractor_1_out), .bin(Cin), .bout(subtractor_1_bout));
  assign F = add ? adder_1_out : 16'bz;  // Controlled_Buffer controlled_buffer_1
  assign Cout = add ? adder_1_cout : 1'bz;  // Controlled_Buffer controlled_buffer_2
  assign F = sub ? subtractor_1_out : 16'bz;  // Controlled_Buffer controlled_buffer_3
  assign Cout = sub ? subtractor_1_bout : 1'bz;  // Controlled_Buffer controlled_buffer_4
  assign and_1_out = A & B;  // AND_Gate and_1, 16 bits wide
  assign F = \and  ? and_1_out : 16'bz;  // Controlled_Buffer controlled_buffer_5
endmodule

module MP16_16b (
  input  [3:0] I0,
  input  [3:0] I1,
  input  [3:0] I2,
  input  [3:0] I3,
  input  [3:0] I4,
  input  [3:0] I5,
  input  [3:0] I6,
  input  [3:0] I7,
  input  [3:0] I8,
  input  [3:0] I9,
  input  [3:0] I10,
  input  [3:0] I11,
  input  [3:0] I12,
  input  [3:0] I13,
  input  [3:0] I14,
  input  [3:0] I15,
  input  En,
  input  S0,
  input  S1,
  input  S2,
  input  S3,
  output [3:0] OUT
);

  wire [3:0] mp2_4b_1_y, mp2_4b_2_y, mp2_4b_3_y, mp2_4b_4_y, mp2_4b_5_y, mp2_4b_6_y, mp2_4b_7_y, mp2_4b_9_y,
       mp2_4b_10_y, mp2_4b_11_y, mp2_4b_12_y, mp2_4b_13_y, mp2_4b_14_y, mp2_4b_15_y;

  MP2_4b mp2_4b_1 (.En(En), .in_2(I0), .in_3(I1), .S0(S0), .Y(mp2_4b_1_y));
  MP2_4b mp2_4b_2 (.in_2(mp2_4b_1_y), .in_3(mp2_4b_3_y), .S0(S1), .Y(mp2_4b_2_y));  // open: En
  MP2_4b mp2_4b_3 (.En(En), .in_2(I2), .in_3(I3), .S0(S0), .Y(mp2_4b_3_y));
  MP2_4b mp2_4b_4 (.En(En), .in_2(mp2_4b_2_y), .in_3(mp2_4b_6_y), .S0(S2), .Y(mp2_4b_4_y));
  MP2_4b mp2_4b_5 (.En(En), .in_2(I4), .in_3(I5), .S0(S0), .Y(mp2_4b_5_y));
  MP2_4b mp2_4b_6 (.in_2(mp2_4b_5_y), .in_3(mp2_4b_7_y), .S0(S1), .Y(mp2_4b_6_y));  // open: En
  MP2_4b mp2_4b_7 (.En(En), .in_2(I6), .in_3(I7), .S0(S0), .Y(mp2_4b_7_y));
  MP2_4b mp2_4b_8 (.En(En), .in_2(mp2_4b_4_y), .in_3(mp2_4b_12_y), .S0(S3), .Y(OUT));
  MP2_4b mp2_4b_9 (.En(En), .in_2(I8), .in_3(I9), .S0(S0), .Y(mp2_4b_9_y));
  MP2_4b mp2_4b_10 (.in_2(mp2_4b_9_y), .in_3(mp2_4b_11_y), .S0(S1), .Y(mp2_4b_10_y));  // open: En
  MP2_4b mp2_4b_11 (.En(En), .in_2(I10), .in_3(I11), .S0(S0), .Y(mp2_4b_11_y));
  MP2_4b mp2_4b_12 (.En(En), .in_2(mp2_4b_10_y), .in_3(mp2_4b_14_y), .S0(S2), .Y(mp2_4b_12_y));
  MP2_4b mp2_4b_13 (.En(En), .in_2(I12), .in_3(I13), .S0(S0), .Y(mp2_4b_13_y));
  MP2_4b mp2_4b_14 (.in_2(mp2_4b_13_y), .in_3(mp2_4b_15_y), .S0(S1), .Y(mp2_4b_14_y));  // open: En
  MP2_4b mp2_4b_15 (.En(En), .in_2(I14), .in_3(I15), .S0(S0), .Y(mp2_4b_15_y));

  // Other names for the same wires on the sheet: enn = En
endmodule

module ROM16x19 (
  input  [3:0] A3__0,
  input  CS,
  output [18:0] DOUT
);

  ROM #(.addrWidth(4), .dataWidth(19)) rom_1 (.addr(A3__0), .data(DOUT), .sel(CS));

  // Notes on the sheet:
  //   contents of rom_1 (hex, n*v repeats v):
  //   2000 63000 1f 1c020 5b 2c020 5f 3c020 80 103 54208 c 1c00
endmodule

// 6
module ROM64X38 (
  input  [5:0] A5__0,
  input  CS,
  output [31:0] DOUT31__0,
  output [7:0] DOUT39__32
);

  ROM #(.addrWidth(6)) rom_1 (.addr(A5__0), .data(DOUT39__32), .sel(CS));
  ROM #(.addrWidth(6), .dataWidth(32)) rom_2 (.addr(A5__0), .data(DOUT31__0), .sel(CS));

  // Notes on the sheet:
  //   contents of rom_1 (hex, n*v repeats v):
  //   2 3 94 0 0 15 94 0 0 25 0 2d c 94 0 95 0 45 0 4d 3c 97 94 0 94 76 0 6d 94 94 60 60 94 0 89 94 64
  //   contents of rom_2 (hex, n*v repeats v):
  //   0 80000000 80000001 2 c 4000010 80000060 2 e 4000010 7800078c 4000810 80010000 80000800 1800
  //   80000000 200c 4000010 200c 4000 80008000 0 80000040 20010000 80000180 80000000 44020000 4000
  //   80000000 80000800 80050000 80090600 81000780 10006c 4000010 80200040 82000000 80c00000
endmodule
