// Logisim project MAINProject.circ as structural Verilog: 8 circuits, main circuit COMPUTER
module COMPUTER (
);

  wire BTN_INTR0_out, BTN_INTR1_out, BTN_INTR2_out, BTN_INTR3_out, BTN_INTR4_out, BTN_INTR5_out,
       BTN_INTR6_out, BTN_INTR7_out, BTN_RST_out, CLK, cpu_1_inta, pull_resistor_2_node,
       pull_resistor_6_node, ram_1_out_8, rst;
  wire [2:0] cpu_1_uext2__0;
  wire [7:0] interrupt_interface_8_1_intr7__0;
  wire [15:0] pull_resistor_3_node, pull_resistor_4_node, ram_1_out_7;

  Button BTN_RST (.out(BTN_RST_out));
  Clock u_CLK (.out(CLK));
  RisingEdge risingedge_1 (.INPUT(BTN_RST_out), .CLK(CLK), .OUTPUT(rst));
  RAM ram_1 (
    .in_1(pull_resistor_3_node), .in_2(CLK), .in_3(pull_resistor_4_node), .in_4(pull_resistor_2_node),
    .in_5(pull_resistor_6_node), .in_6(rst), .out_7(ram_1_out_7), .out_8(ram_1_out_8));
  Pull_Resistor pull_resistor_1 (.node(ram_1_out_7));
  Pull_Resistor pull_resistor_2 (.node(pull_resistor_2_node));
  Pull_Resistor pull_resistor_3 (.node(pull_resistor_3_node));
  Pull_Resistor pull_resistor_4 (.node(pull_resistor_4_node));
  Pull_Resistor pull_resistor_5 (.node(ram_1_out_8));
  Pull_Resistor pull_resistor_6 (.node(pull_resistor_6_node));
  CPU cpu_1 (
    .in_1(rst), .in_2(CLK), .in_3(ram_1_out_8), .in_4(ram_1_out_7), .ABUS(pull_resistor_3_node),
    .DOUTBUS(pull_resistor_4_node), .out_8(pull_resistor_2_node), .out_9(pull_resistor_6_node),
    .inta(cpu_1_inta), .intr7__0(interrupt_interface_8_1_intr7__0), .UEXT2__0(cpu_1_uext2__0));
  INTERRUPT_INTERFACE_8 interrupt_interface_8_1 (
    .BTN_INTR0(BTN_INTR0_out), .BTN_INTR1(BTN_INTR1_out), .BTN_INTR2(BTN_INTR2_out),
    .BTN_INTR3(BTN_INTR3_out), .BTN_INTR4(BTN_INTR4_out), .BTN_INTR5(BTN_INTR5_out),
    .BTN_INTR6(BTN_INTR6_out), .BTN_INTR7(BTN_INTR7_out), .inta(cpu_1_inta), .UEXT2__0(cpu_1_uext2__0),
    .CLK(CLK), .intr7__0(interrupt_interface_8_1_intr7__0));
  Button BTN_INTR7 (.out(BTN_INTR7_out));
  Button BTN_INTR6 (.out(BTN_INTR6_out));
  Button BTN_INTR5 (.out(BTN_INTR5_out));
  Button BTN_INTR4 (.out(BTN_INTR4_out));
  Button BTN_INTR3 (.out(BTN_INTR3_out));
  Button BTN_INTR2 (.out(BTN_INTR2_out));
  Button BTN_INTR1 (.out(BTN_INTR1_out));
  Button BTN_INTR0 (.out(BTN_INTR0_out));
endmodule

module CPU (
  input  in_1,
  input  in_2,
  input  in_3,
  input  [15:0] in_4,
  input  [7:0] intr7__0,
  output [15:0] ABUS,
  output [15:0] DOUTBUS,
  output out_8,
  output out_9,
  output inta,
  output [2:0] UEXT2__0
);

  wire common_1_grinst, XXR0;
  wire [3:0] common_1_phaseffbus;
  wire [6:0] common_1_addrbus;
  wire [7:0] pull_resistor_3_node, pull_resistor_5_node;
  wire [11:0] pull_resistor_7_node;
  wire [14:0] pull_resistor_6_node;
  wire [15:0] A, ALU, B15__0, INTRADDR, PSW;
  wire [19:0] common_1_instrucbus;

  COMMON common_1 (
    .CLK(in_2), .RST(in_1), .DIN(in_4), .CMEMBUS(pull_resistor_6_node), .MAR(ABUS), .MDR(DOUTBUS),
    .PHASEFFBUS(common_1_phaseffbus), .INSTRUCBUS(common_1_instrucbus), .ADDRBUS(common_1_addrbus),
    .PSW(PSW), .CREGBUS(pull_resistor_7_node), .CFFBUS(pull_resistor_5_node), .B(B15__0), .A(A),
    .CPSW(pull_resistor_3_node), .ALU(ALU), .IVTPPDSP(INTRADDR), .ISXR0(XXR0), .grinst(common_1_grinst));
  Pull_Resistor pull_resistor_1 (.node(common_1_phaseffbus));
  Pull_Resistor pull_resistor_2 (.node(common_1_instrucbus));
  Pull_Resistor pull_resistor_3 (.node(pull_resistor_3_node));
  Pull_Resistor pull_resistor_4 (.node(common_1_addrbus));
  Pull_Resistor pull_resistor_5 (.node(pull_resistor_5_node));
  Pull_Resistor pull_resistor_6 (.node(pull_resistor_6_node));
  Pull_Resistor pull_resistor_7 (.node(pull_resistor_7_node));
  FETCH fetch_1 (
    .in_1(in_1), .in_2(in_2), .in_3(in_3), .PHASEFFBUS(common_1_phaseffbus),
    .INSTRUCBUS(common_1_instrucbus), .ADDRBUS(common_1_addrbus), .PSW(PSW), .rdMEM(out_9),
    .CMEMBUS(pull_resistor_6_node), .CREGBUS(pull_resistor_7_node), .CFFBUS(pull_resistor_5_node),
    .in_4(common_1_grinst));
  ADDR addr_1 (
    .in_1(in_1), .in_2(in_2), .in_3(in_3), .PHASEFFBUS(common_1_phaseffbus),
    .INSTRUCBUS(common_1_instrucbus), .ADDRBUS(common_1_addrbus), .CMEMBUS(pull_resistor_6_node),
    .CFFBUS(pull_resistor_5_node), .CREGBUS(pull_resistor_7_node), .rdMEM(out_9));
  EXEC exec_1 (
    .in_1(in_1), .in_2(in_2), .in_3(in_3), .B(B15__0), .PHASEFFBUS(common_1_phaseffbus),
    .INSTRUCBUS(common_1_instrucbus), .ADDRBUS(common_1_addrbus), .PSW(PSW), .A(A), .ALU(ALU),
    .CMEMBUS(pull_resistor_6_node), .CFFBUS(pull_resistor_5_node), .CREGBUS(pull_resistor_7_node),
    .CPSW(pull_resistor_3_node), .rdMEM(out_9), .wrMEM(out_8), .in_9(XXR0), .MDR(DOUTBUS));
  INTR intr_1 (
    .in_1(in_1), .in_2(in_2), .in_3(in_3), .PHASEFFBUS(common_1_phaseffbus),
    .INSTRUCBUS(common_1_instrucbus), .PSW(PSW), .intr(intr7__0), .ADDIVTP(INTRADDR),
    .CMEMBUS(pull_resistor_6_node), .CFFBUS(pull_resistor_5_node), .CREGBUS(pull_resistor_7_node),
    .rdMEM(out_9), .wrMEM(out_8), .UEXT2__0(UEXT2__0), .inta(inta));

  // Other names for the same wires on the sheet: CLK = in_2; DIN15__0[15:0] = in_4; FCBUS = in_3; MAR[15:0] = ABUS;
  //   MDR[15:0] = DOUTBUS; RD = out_9; rst = in_1; WR = out_8
endmodule

module COMMON (
  input  CLK,
  input  RST,
  input  [15:0] DIN,
  input  [15:0] A,
  input  [15:0] ALU,
  input  [15:0] IVTPPDSP,
  input  [14:0] CMEMBUS,
  input  [7:0] CFFBUS,
  input  [11:0] CREGBUS,
  input  [7:0] CPSW,
  output [15:0] MAR,
  output [15:0] MDR,
  output [3:0] PHASEFFBUS,
  output [19:0] INSTRUCBUS,
  output [6:0] ADDRBUS,
  output [15:0] PSW,
  output [15:0] B,
  output ISXR0,
  output grinst
);

  wire ACCINST, adrinst, and_1_out, and_4_out, and_5_out, and_6_out, and_7_out, and_8_out, and_9_out,
       and_10_out, and_11_out, and_12_out, and_13_out, and_14_out, and_15_out, and_16_out, and_17_out,
       and_18_out, and_19_out, and_20_out, and_21_out, and_22_out, and_23_out, and_24_out, and_25_out,
       and_26_out, and_27_out, and_28_out, and_29_out, and_30_out, ARINST, bezadrinst, branchinst, C, GKO,
       GNA, GNA7, GNA8, GNA9, GNA10, GNA11, GNA12, GNA13, GNA14, GNA15, GNKOKINA, GOK0, GOK1, GOK2, GOK5,
       GOK6, GOK7, GOK9, GOK10, GOK11, GOK13, GOK14, GOK15, GOKADR, GOKADR7, GOKADR8, GOKADR9, GOKADR10,
       GOKADR11, GOKADR12, GOKADR13, GOKADR14, GOKADR15, GOKBEZADR, GOKBEZADR3, GOKBEZADR10, GOKBEZADR11,
       GOKBEZADR12, GOKBEZADR13, GOKBEZADR14, GOKBEZADR15, GOKBRNCH, GOKBRNCH3, GOKBRNCH5, GOKBRNCH6,
       GOKBRNCH7, GOKBRNCH8, GOKBRNCH9, GOKBRNCH10, GOKBRNCH11, GOKBRNCH12, GOKBRNCH13, GOKBRNCH14,
       GOKBRNCH15, GOKJMP, GPOCKO, INST, jmpinst, nor_3_out, nor_4_out, not_1_out, not_2_out, not_3_out,
       not_4_out, not_5_out, not_6_out, not_7_out, not_8_out, not_9_out, not_10_out, not_11_out, or_10_out,
       or_11_out, or_14_out, or_15_out, or_16_out, or_17_out, or_18_out, or_19_out, or_21_out, or_22_out,
       or_23_out, SS0, SS1, SS2, SS3;
  wire [3:0] IR19__16, mp16_16b_1_out;
  wire [7:4] IR23__16;
  wire [11:8] IR27__16;
  wire [15:0] add16_2_f, ADDW15__0, IR15__0, mp2_16b_1_out_5, mp2_16b_2_out_5, mp2_16b_3_out_5, mp4_16b_1_y,
       mp4_16b_2_y, mp4_16b_3_y, mp8_16b_1_y, PC15__0, R15__0, R31__16, SP15__0;
  wire [15:12] IR31__16;

  MP16_16b mp16_16b_1 (
    .En(1'b1), .S0(SS0), .S1(SS1), .S2(SS2), .S3(SS3), .I0(4'b0000), .I1(4'b0001), .I2(4'b0010),
    .I3(4'b0011), .I4(4'b0100), .I5(4'b0101), .I6(4'b0110), .I7(4'b0111), .I8(4'b1000), .I9(4'b1001),
    .OUT(mp16_16b_1_out));  // open: I10, I11, I12, I13, I14, I15
  ADD16 add16_1 (.A({{9{IR15__0[15]}}, IR15__0[14:8]}), .B(mp2_16b_1_out_5), .F(ADDW15__0), .C16(C));  // open: C0
  MP2_16b mp2_16b_1 (.En(1'b1), .in_2(mp2_16b_2_out_5), .in_3(add16_2_f), .S0(ADDRBUS[6]), .out_5(mp2_16b_1_out_5));
  DRF2x32 drf2x32_1 (.DI15__0(A), .A3__0(mp16_16b_1_out), .WR(CREGBUS[5]), .CLK(CLK), .DO31__0({R31__16, R15__0}));
  MP2_16b mp2_16b_2 (.En(1'b1), .in_2(R15__0), .in_3(R31__16), .S0(ADDRBUS[5]), .out_5(mp2_16b_2_out_5));
  or or_1 (GPOCKO, GOK0, GOK1, GOK2, GOK5, GOK6, GOK7, GOK9, GOK10, GOK11, GOK13, GOK14, GOK15);
  or or_2 (GOKBRNCH, GOKBRNCH3, GOKBRNCH5, GOKBRNCH6, GOKBRNCH7, GOKBRNCH8, GOKBRNCH9, GOKBRNCH10, GOKBRNCH11, GOKBRNCH12, GOKBRNCH13, GOKBRNCH14, GOKBRNCH15);
  or or_3 (GKO, GPOCKO, GOKBEZADR, GOKBRNCH, GOKADR, GOKJMP);
  ADD16 add16_2 (.A(R31__16), .B(R15__0), .F(add16_2_f));  // open: C0, C16
  or or_4 (SS3, CREGBUS[10], CREGBUS[9]);
  or or_5 (SS2, INSTRUCBUS[6], INSTRUCBUS[5], INSTRUCBUS[4], INSTRUCBUS[3]);
  or or_6 (GOKBEZADR, GOKBEZADR3, GOKBEZADR10, GOKBEZADR11, GOKBEZADR12, GOKBEZADR13, GOKBEZADR14, GOKBEZADR15);
  or or_7 (GOKADR, GOKADR7, GOKADR8, GOKADR9, GOKADR10, GOKADR11, GOKADR12, GOKADR13, GOKADR14, GOKADR15);
  or or_8 (grinst, GNKOKINA, GNA, GKO);
  or or_9 (SS1, INSTRUCBUS[8], INSTRUCBUS[6], INSTRUCBUS[4], ADDRBUS[2], ADDRBUS[3]);
  MP8_16b mp8_16b_1 (
    .En(1'b1), .S0(CMEMBUS[6]), .S1(CMEMBUS[7]), .S2(CMEMBUS[8]), .I0(PC15__0), .I1(IR15__0), .I2(R15__0),
    .I3(ADDW15__0), .I4(SP15__0), .I5(R31__16), .I6(IVTPPDSP), .Y(mp8_16b_1_y));  // open: I7
  REG16_INC_LD reg16_inc_ld_1 (
    .I15__0(mp8_16b_1_y), .LD(CMEMBUS[0]), .INC(CMEMBUS[5]), .CLK(CLK), .A15__0(MAR));  // open: mr
  REG16_LD reg16_ld_1 (
    .I15__0(MDR), .LD(CREGBUS[0]), .CLK(CLK), .A15__0({IR31__16, IR27__16, IR23__16, IR19__16}));  // open: mr
  and and_1 (and_1_out, or_10_out, IR19__16[0]);
  or or_10 (or_10_out, ADDRBUS[4], ADDRBUS[6], ADDRBUS[5]);
  DC4_16 dc4_16_1 (
    .En(PSW[0]), .X3__0(IR31__16), .D0(GOK0), .D1(GOK1), .D2(GOK2), .D3(adrinst), .D4(jmpinst), .D5(GOK5),
    .D6(GOK6), .D7(GOK7), .D8(bezadrinst), .D9(GOK9), .D10(GOK10), .D11(GOK11), .D12(branchinst),
    .D13(GOK13), .D14(GOK14), .D15(GOK15));
  nor nor_1 (INSTRUCBUS[12], ~jmpinst, IR27__16[11], IR27__16[10], IR27__16[9], IR27__16[8]);  // NOR_Gate
  or or_11 (or_11_out, INSTRUCBUS[14], INSTRUCBUS[19]);
  or or_12 (SS0, INSTRUCBUS[6], ADDRBUS[3], and_1_out, INSTRUCBUS[5], INSTRUCBUS[8], CREGBUS[10]);
  not not_1 (not_1_out, INSTRUCBUS[12]);
  and and_2 (GOKJMP, not_1_out, jmpinst);
  and and_3 (GNKOKINA, or_11_out, ADDRBUS[0]);
  or or_13 (GNA, GNA7, GNA8, GNA9, GNA10, GNA11, GNA12, GNA13, GNA14, GNA15);
  REG16_LD reg16_ld_2 (.I15__0(MDR), .LD(CREGBUS[1]), .CLK(CLK), .A15__0(IR15__0));  // open: mr
  nor nor_2 (ISXR0, R31__16[15], R31__16[14], R31__16[13], R31__16[12], R31__16[11], R31__16[10], R31__16[9], R31__16[8], R31__16[7], R31__16[6], R31__16[5], R31__16[4], R31__16[3], R31__16[2], R31__16[1], R31__16[0]);
  MP4_16b mp4_16b_1 (
    .En(1'b1), .S0(CMEMBUS[9]), .S1(CMEMBUS[10]), .I0(DIN), .I1(A), .I2(PC15__0), .I3(PSW), .Y(mp4_16b_1_y));
  REG16_LD reg16_ld_3 (.I15__0(mp4_16b_1_y), .LD(CMEMBUS[2]), .CLK(CLK), .A15__0(MDR));  // open: mr
  DC4_16 dc4_16_2 (
    .En(bezadrinst), .X3__0(IR27__16), .D0(INSTRUCBUS[0]), .D1(INSTRUCBUS[1]), .D2(INSTRUCBUS[2]),
    .D3(GOKBEZADR3), .D4(INSTRUCBUS[3]), .D5(INSTRUCBUS[4]), .D6(INSTRUCBUS[5]), .D7(INSTRUCBUS[6]),
    .D8(INSTRUCBUS[7]), .D9(INSTRUCBUS[8]), .D10(GOKBEZADR10), .D11(GOKBEZADR11), .D12(GOKBEZADR12),
    .D13(GOKBEZADR13), .D14(GOKBEZADR14), .D15(GOKBEZADR15));
  DC4_16 dc4_16_3 (
    .En(adrinst), .X3__0(IR27__16), .D0(INSTRUCBUS[13]), .D1(INSTRUCBUS[14]), .D2(INSTRUCBUS[15]),
    .D3(INSTRUCBUS[16]), .D4(INSTRUCBUS[17]), .D5(INSTRUCBUS[18]), .D6(INSTRUCBUS[19]), .D7(GOKADR7),
    .D8(GOKADR8), .D9(GOKADR9), .D10(GOKADR10), .D11(GOKADR11), .D12(GOKADR12), .D13(GOKADR13),
    .D14(GOKADR14), .D15(GOKADR15));
  MP4_16b mp4_16b_2 (
    .En(1'b1), .S0(CMEMBUS[11]), .S1(CMEMBUS[12]), .I0(IR15__0), .I1(B), .I2(MDR), .Y(mp4_16b_2_y));  // open: I3
  REG16 reg16_1 (
    .LD(RST), .A(16'hf000), .DEC(CREGBUS[8]), .INC(CREGBUS[7]), .CLK(CLK), .I(SP15__0));  // open: CL, SL, IL, SR, IR, Cout, Eout, mr
  not not_2 (not_2_out, RST);
  RSFF rsff_1 (.S(CFFBUS[0]), .CLK(CLK), .R(CFFBUS[1]), .Sd(not_2_out), .Rd(1'b1), .Q(PHASEFFBUS[0]));  // open: notQ
  MP2_16b mp2_16b_3 (.En(1'b1), .in_2(mp4_16b_2_y), .in_3(16'h1000), .S0(RST), .out_5(mp2_16b_3_out_5));
  REG16_INC_LD reg16_inc_ld_2 (
    .I15__0(mp2_16b_3_out_5), .LD(or_14_out), .INC(CMEMBUS[1]), .CLK(CLK), .A15__0(PC15__0));  // open: mr
  or or_14 (or_14_out, CMEMBUS[4], RST);
  DC4_16 dc4_16_4 (
    .En(branchinst), .X3__0(IR27__16), .D1(INSTRUCBUS[9]), .D2(INSTRUCBUS[10]), .D3(GOKBRNCH3),
    .D4(INSTRUCBUS[11]), .D5(GOKBRNCH5), .D6(GOKBRNCH6), .D7(GOKBRNCH7), .D8(GOKBRNCH8), .D9(GOKBRNCH9),
    .D10(GOKBRNCH10), .D11(GOKBRNCH11), .D12(GOKBRNCH12), .D13(GOKBRNCH13), .D14(GOKBRNCH14), .D15(GOKBRNCH15));  // open: D0
  DC4_16 dc4_16_5 (
    .En(adrinst), .X3__0(IR23__16), .D0(ADDRBUS[0]), .D1(ADDRBUS[1]), .D2(ADDRBUS[2]), .D3(ADDRBUS[3]),
    .D4(ADDRBUS[4]), .D5(ADDRBUS[5]), .D6(ADDRBUS[6]), .D7(GNA7), .D8(GNA8), .D9(GNA9), .D10(GNA10),
    .D11(GNA11), .D12(GNA12), .D13(GNA13), .D14(GNA14), .D15(GNA15));
  RSFF rsff_2 (.S(CFFBUS[2]), .CLK(CLK), .R(CFFBUS[3]), .Sd(1'b1), .Rd(not_3_out), .Q(PHASEFFBUS[1]));  // open: notQ
  not not_3 (not_3_out, RST);
  and and_4 (and_4_out, ~ALU[15], A[15], B[15]);  // AND_Gate
  and and_5 (and_5_out, ALU[15], ~A[15], ~B[15]);  // AND_Gate
  and and_6 (and_6_out, ~ALU[15], ~B[15], A[15]);  // AND_Gate
  and and_7 (and_7_out, ALU[15], B[15], ~A[15]);  // AND_Gate
  RSFF rsff_3 (.S(CFFBUS[4]), .CLK(CLK), .R(CFFBUS[5]), .Sd(1'b1), .Rd(not_4_out), .Q(PHASEFFBUS[2]));  // open: notQ
  not not_4 (not_4_out, RST);
  and and_8 (and_8_out, MDR[0], CPSW[0]);
  or or_15 (or_15_out, and_4_out, and_5_out);
  or or_16 (or_16_out, and_6_out, and_7_out);
  and and_9 (and_9_out, MDR[2], INSTRUCBUS[2]);
  or or_17 (or_17_out, and_9_out, and_10_out);
  and and_10 (and_10_out, C, ARINST);
  nor nor_3 (nor_3_out, ALU[0], ALU[1], ALU[2], ALU[3], ALU[4], ALU[5], ALU[6], ALU[7], ALU[8], ALU[9], ALU[10], ALU[11], ALU[12], ALU[13], ALU[14], ALU[15]);
  nor nor_4 (nor_4_out, A[0], A[1], A[2], A[3], A[4], A[5], A[6], A[7], A[8], A[9], A[10], A[11], A[12], A[13], A[14], A[15]);
  and and_11 (and_11_out, MDR[4], INSTRUCBUS[2]);
  and and_12 (and_12_out, ACCINST, A[15]);
  and and_13 (and_13_out, INSTRUCBUS[17], ALU[15]);
  and and_14 (and_14_out, MDR[15], INSTRUCBUS[2]);
  not not_5 (not_5_out, RST);
  RSFF rsff_4 (.S(or_18_out), .CLK(CLK), .R(CPSW[6]), .Sd(not_5_out), .Rd(1'b1), .Q(PSW[0]));  // open: notQ
  or or_18 (or_18_out, CPSW[5], and_8_out);
  and and_15 (and_15_out, INSTRUCBUS[16], or_15_out);
  or or_19 (or_19_out, and_15_out, and_16_out);
  and and_16 (and_16_out, INSTRUCBUS[17], or_16_out);
  or or_20 (INST, ARINST, INSTRUCBUS[13]);
  and and_17 (and_17_out, nor_3_out, INSTRUCBUS[17]);
  and and_18 (and_18_out, nor_4_out, ACCINST);
  or or_21 (or_21_out, and_11_out, and_12_out, and_13_out);
  and and_19 (and_19_out, MDR[1], INSTRUCBUS[2]);
  or or_22 (or_22_out, and_19_out, or_19_out);
  and and_20 (and_20_out, MDR[3], INSTRUCBUS[2]);
  or or_23 (or_23_out, and_20_out, and_17_out, and_18_out);
  and and_21 (and_21_out, ~and_14_out, CPSW[7]);  // AND_Gate
  and and_22 (and_22_out, CPSW[7], and_14_out);
  RSFF rsff_5 (.S(CFFBUS[6]), .CLK(CLK), .R(CFFBUS[7]), .Sd(1'b1), .Rd(not_6_out), .Q(PHASEFFBUS[3]));  // open: notQ
  not not_6 (not_6_out, RST);
  and and_23 (and_23_out, ~or_17_out, CPSW[2]);  // AND_Gate
  and and_24 (and_24_out, CPSW[2], or_17_out);
  or or_24 (ARINST, INSTRUCBUS[15], INSTRUCBUS[16], INSTRUCBUS[17]);
  and and_25 (and_25_out, ~or_21_out, CPSW[4]);  // AND_Gate
  and and_26 (and_26_out, CPSW[4], or_21_out);
  not not_7 (not_7_out, RST);
  RSFF rsff_6 (.S(and_22_out), .CLK(CLK), .R(and_21_out), .Sd(not_7_out), .Q(PSW[15]));  // open: Rd, notQ
  and and_27 (and_27_out, ~or_22_out, CPSW[1]);  // AND_Gate
  and and_28 (and_28_out, CPSW[1], or_22_out);
  RSFF rsff_7 (.S(and_24_out), .CLK(CLK), .R(and_23_out), .Rd(not_8_out), .Q(PSW[2]));  // open: Sd, notQ
  not not_8 (not_8_out, RST);
  or or_25 (ACCINST, INSTRUCBUS[15], INSTRUCBUS[16], INSTRUCBUS[13]);
  and and_29 (and_29_out, ~or_23_out, CPSW[3]);  // AND_Gate
  and and_30 (and_30_out, CPSW[3], or_23_out);
  RSFF rsff_8 (.S(and_26_out), .CLK(CLK), .R(and_25_out), .Rd(not_9_out), .Q(PSW[4]));  // open: Sd, notQ
  not not_9 (not_9_out, RST);
  RSFF rsff_9 (.S(and_28_out), .CLK(CLK), .R(and_27_out), .Rd(not_10_out), .Q(PSW[1]));  // open: Sd, notQ
  not not_10 (not_10_out, RST);
  RSFF rsff_10 (.S(and_30_out), .CLK(CLK), .R(and_29_out), .Rd(not_11_out), .Q(PSW[3]));  // open: Sd, notQ
  not not_11 (not_11_out, RST);
  MP4_16b mp4_16b_3 (
    .En(1'b1), .S0(CREGBUS[3]), .S1(CREGBUS[4]), .I0(MDR), .I1(IR15__0), .I2(R15__0), .Y(mp4_16b_3_y));  // open: I3
  REG16_CL_LD reg16_cl_ld_1 (
    .I15__0(mp4_16b_3_y), .CL(CREGBUS[6]), .LD(CREGBUS[2]), .CLK(CLK), .A15__0(B));  // open: mr

  // Other names for the same wires on the sheet: A15__0[15:0] = A; immed = ADDRBUS[0]; memdir = ADDRBUS[1];
  //   regdir = ADDRBUS[2]; regind = ADDRBUS[3]; brpom = ADDRBUS[4]; xrpom = ADDRBUS[5]; bxpom = ADDRBUS[6];
  //   ALU15__0[15:0] = ALU; B15__0[15:0] = B; stFETCH = CFFBUS[0]; clFETCH = CFFBUS[1]; stADDR = CFFBUS[2];
  //   clADDR = CFFBUS[3]; stEXEC = CFFBUS[4]; clEXEC = CFFBUS[5]; stINTR = CFFBUS[6]; clINTR = CFFBUS[7];
  //   ldMAR = CMEMBUS[0]; incPC = CMEMBUS[1]; ldMDR = CMEMBUS[2]; ldPC = CMEMBUS[4]; incMAR = CMEMBUS[5];
  //   mxMAR0 = CMEMBUS[6]; mxMAR1 = CMEMBUS[7]; mxMAR2 = CMEMBUS[8]; mxMDR0 = CMEMBUS[9]; mxMDR1 = CMEMBUS[10];
  //   mxPC0 = CMEMBUS[11]; mxPC1 = CMEMBUS[12]; ldPSWSTART = CPSW[0]; ldV = CPSW[1]; ldC = CPSW[2]; ldZ = CPSW[3];
  //   ldN = CPSW[4]; stPSWSTART = CPSW[5]; clPSWSTART = CPSW[6]; ldI = CPSW[7]; ldIR31__16 = CREGBUS[0];
  //   ldIR15__0 = CREGBUS[1]; ldB = CREGBUS[2]; mxB0 = CREGBUS[3]; mxB1 = CREGBUS[4]; wrRF = CREGBUS[5];
  //   clB = CREGBUS[6]; incSP = CREGBUS[7]; decSP = CREGBUS[8]; setpointer = CREGBUS[9]; incpointer = CREGBUS[10];
  //   Din15__0[15:0] = DIN; ENTRADDR15__0[15:0] = IVTPPDSP; HALT = INSTRUCBUS[0]; RTS = INSTRUCBUS[1];
  //   RTI = INSTRUCBUS[2]; STBR0 = INSTRUCBUS[3]; STXR0 = INSTRUCBUS[4]; STBR1 = INSTRUCBUS[5]; STXR1 = INSTRUCBUS[6];
  //   STRCPY = INSTRUCBUS[7]; STAR = INSTRUCBUS[8]; JNEQ = INSTRUCBUS[9]; JLSSU = INSTRUCBUS[10];
  //   JLSS = INSTRUCBUS[11]; JMP = INSTRUCBUS[12]; LD = INSTRUCBUS[13]; ST = INSTRUCBUS[14]; AND = INSTRUCBUS[15];
  //   ADD = INSTRUCBUS[16]; CMP = INSTRUCBUS[17]; JSR = INSTRUCBUS[18]; CLR = INSTRUCBUS[19];
  //   IR23__16[3:0] = IR19__16; IR27__16[7:0] = {IR23__16, IR19__16}; IR31__16[11:0] = {IR27__16, IR23__16, IR19__16};
  //   MAR15__0[15:0] = MAR; MDR15__0[15:0] = MDR; FETCH = PHASEFFBUS[0]; ADDR = PHASEFFBUS[1]; EXEC = PHASEFFBUS[2];
  //   INTR = PHASEFFBUS[3]; PSW15__0[15:0] = PSW; PSWSTART = PSW[0]; PSWV = PSW[1]; PSWC = PSW[2]; PSWZ = PSW[3];
  //   PSWN = PSW[4]; PSWI = PSW[15]

  // Notes on the sheet:
  //   incpointer
  //   setpointer
  //   XR[1]
  //   XR[0]
  //   BR[1]
  //   BR[0]
  //   AR
  //   DR
  //   R[1]
  //   R[0]
  //   Adder
  //    Scheme of grinst signal formation
  //   Register file
  //   Instruction register IR
  //   MAR (Memory adress register)
  //   Decoders for recognizing instructions based on the contents of register IR23..16
  //   MDR (Memory data register)
  //   PC (Program counter)
  //   SP (Stack Pointer)
  //   FlipFlops to start the FETCH, ADDR, EXEC and INTR phases of instruction execution
  //   Program status word (PSW)
  //   BIT PSWSTART
  //   BIT C
  //   BIT N
  //   BIT I
  //   BIT V
  //   BIT Z
  //   Operand Register (B)
endmodule

module FETCH (
  input  in_1,
  input  in_2,
  input  in_3,
  input  in_4,
  input  [3:0] PHASEFFBUS,
  input  [19:0] INSTRUCBUS,
  input  [6:0] ADDRBUS,
  input  [15:0] PSW,
  output [14:0] CMEMBUS,
  output [7:0] CFFBUS,
  output [11:0] CREGBUS,
  output rdMEM
);

  wire adr2, and_2_out, and_3_out, and_4_out, and_5_out, and_6_out, and_7_out, and_8_out, bezadr2, bradr2,
       branch4, brbezadr2, brbranch4, brcnd, brgrinst, brjmp4, brnotFCBUS, bruncnd, clFETCH, incPC,
       ldIR15__0, ldIR31__16, ldMAR, ldMDR, not_1_out, not_2_out, not_3_out, not_4_out, not_5_out,
       notPSWSTARTandFETCH, or_3_out, or_4_out, or_5_out, or_6_out, rdMEM_t, stADDR, stEXEC;
  wire [3:0] reg4_inc_ld_1_a3__0, rom_16x17_1_dout, rom_16x17_1_dout_2;

  not not_1 (not_1_out, in_1);
  REG4_INC_LD reg4_inc_ld_1 (
    .I3__0(rom_16x17_1_dout_2), .LD(or_3_out), .INC(not_2_out), .mr(not_1_out), .CLK(in_2),
    .A3__0(reg4_inc_ld_1_a3__0));
  or or_1 (bezadr2, INSTRUCBUS[0], INSTRUCBUS[1], INSTRUCBUS[2], INSTRUCBUS[3], INSTRUCBUS[4], INSTRUCBUS[5], INSTRUCBUS[6], INSTRUCBUS[7], INSTRUCBUS[8]);
  not not_2 (not_2_out, or_3_out);
  ROM_16x17 rom_16x17_1 (
    .A3__0(reg4_inc_ld_1_a3__0), .CS(1'b1),
    .DOUT({rom_16x17_1_dout_2, rom_16x17_1_dout, stEXEC, stADDR, clFETCH, ldIR15__0, ldIR31__16, rdMEM_t, ldMDR, incPC, ldMAR}));
  DC4_16 dc4_16_1 (
    .En(1'b1), .X3__0(rom_16x17_1_dout), .D1(bruncnd), .D2(notPSWSTARTandFETCH), .D3(brnotFCBUS),
    .D4(brbezadr2), .D5(bradr2), .D6(brjmp4), .D7(brbranch4), .D8(brgrinst));  // open: D0, D9, D10, D11, D12, D13, D14, D15
  or or_2 (branch4, INSTRUCBUS[9], INSTRUCBUS[10], INSTRUCBUS[11]);
  or or_3 (or_3_out, bruncnd, brcnd);
  or or_4 (or_4_out, INSTRUCBUS[18], INSTRUCBUS[13], INSTRUCBUS[14], INSTRUCBUS[15], INSTRUCBUS[16], INSTRUCBUS[17]);
  or or_5 (or_5_out, ADDRBUS[2], ADDRBUS[3]);
  and and_1 (adr2, or_4_out, or_5_out);
  not not_3 (not_3_out, PHASEFFBUS[0]);
  not not_4 (not_4_out, PSW[0]);
  or or_6 (or_6_out, not_3_out, not_4_out);
  not not_5 (not_5_out, in_3);
  and and_2 (and_2_out, or_6_out, notPSWSTARTandFETCH);
  and and_3 (and_3_out, brnotFCBUS, not_5_out);
  and and_4 (and_4_out, brbezadr2, bezadr2);
  and and_5 (and_5_out, bradr2, adr2);
  and and_6 (and_6_out, brjmp4, INSTRUCBUS[12]);
  and and_7 (and_7_out, brbranch4, branch4);
  and and_8 (and_8_out, brgrinst, in_4);
  or or_7 (brcnd, and_2_out, and_3_out, and_4_out, and_5_out, and_6_out, and_7_out, and_8_out);
  assign CMEMBUS[0] = ldMAR ? 1'b1 : 1'bz;  // Controlled_Buffer controlled_buffer_1
  assign CMEMBUS[1] = incPC ? 1'b1 : 1'bz;  // Controlled_Buffer controlled_buffer_2
  assign CMEMBUS[2] = ldMDR ? 1'b1 : 1'bz;  // Controlled_Buffer controlled_buffer_3
  assign CMEMBUS[3] = rdMEM_t ? 1'b1 : 1'bz;  // Controlled_Buffer controlled_buffer_4
  assign CFFBUS[1] = clFETCH ? 1'b1 : 1'bz;  // Controlled_Buffer controlled_buffer_5
  assign CFFBUS[2] = stADDR ? 1'b1 : 1'bz;  // Controlled_Buffer controlled_buffer_6
  assign CFFBUS[4] = stEXEC ? 1'b1 : 1'bz;  // Controlled_Buffer controlled_buffer_7
  assign CREGBUS[0] = ldIR31__16 ? 1'b1 : 1'bz;  // Controlled_Buffer controlled_buffer_8
  assign CREGBUS[1] = ldIR15__0 ? 1'b1 : 1'bz;  // Controlled_Buffer controlled_buffer_9
  assign rdMEM = rdMEM_t ? 1'b1 : 1'bz;  // Controlled_Buffer controlled_buffer_10

  // Other names for the same wires on the sheet: immed = ADDRBUS[0]; memdir = ADDRBUS[1]; regdir = ADDRBUS[2];
  //   regind = ADDRBUS[3]; brpom = ADDRBUS[4]; xrpom = ADDRBUS[5]; bxpom = ADDRBUS[6]; CLK = in_2; FCBUS = in_3;
  //   grinst = in_4; HALT = INSTRUCBUS[0]; RTS = INSTRUCBUS[1]; RTI = INSTRUCBUS[2]; STBR0 = INSTRUCBUS[3];
  //   STXR0 = INSTRUCBUS[4]; STBR1 = INSTRUCBUS[5]; STXR1 = INSTRUCBUS[6]; STRCPY = INSTRUCBUS[7];
  //   STAR = INSTRUCBUS[8]; JNEQ = INSTRUCBUS[9]; JLSSU = INSTRUCBUS[10]; JLSS = INSTRUCBUS[11]; JMP = INSTRUCBUS[12];
  //   jmp4 = INSTRUCBUS[12]; LD = INSTRUCBUS[13]; ST = INSTRUCBUS[14]; AND = INSTRUCBUS[15]; ADD = INSTRUCBUS[16];
  //   CMP = INSTRUCBUS[17]; JSR = INSTRUCBUS[18]; CLR = INSTRUCBUS[19]; FETCH = PHASEFFBUS[0]; ADDR = PHASEFFBUS[1];
  //   EXEC = PHASEFFBUS[2]; INTR = PHASEFFBUS[3]; PSWSTART = PSW[0]; rst = in_1

  // Notes on the sheet:
  //   Operating unit - FETCH BLOCK
  //   Control unit - FETCH BLOCK
endmodule

module ADDR (
  input  in_1,
  input  in_2,
  input  in_3,
  input  [3:0] PHASEFFBUS,
  input  [19:0] INSTRUCBUS,
  input  [6:0] ADDRBUS,
  output [14:0] CMEMBUS,
  output [7:0] CFFBUS,
  output [11:0] CREGBUS,
  output rdMEM
);

  wire and_1_out, and_2_out, bradr, brcnd, brnotADDR, brnotFCBUS, bruncnd, clADDR, ldB, ldMAR, ldMDR, mxB0,
       mxB1, mxMAR0, mxMAR1, not_1_out, not_2_out, not_3_out, not_4_out, or_1_out, rdMEM_t, stEXEC;
  wire [2:0] rom16x17_1_dout_2;
  wire [3:0] kmadr_1_adr3__0, mp2_4b_1_y, reg4_inc_ld_1_a3__0, rom16x17_1_dout;

  MP2_4b mp2_4b_1 (.En(1'b1), .in_2(rom16x17_1_dout), .in_3(kmadr_1_adr3__0), .S0(bradr), .Y(mp2_4b_1_y));
  not not_1 (not_1_out, in_1);
  REG4_INC_LD reg4_inc_ld_1 (
    .I3__0(mp2_4b_1_y), .LD(or_1_out), .INC(not_2_out), .mr(not_1_out), .CLK(in_2),
    .A3__0(reg4_inc_ld_1_a3__0));
  KMADR kmadr_1 (
    .immed(ADDRBUS[0]), .memdir(ADDRBUS[1]), .regdir(ADDRBUS[2]), .regind(ADDRBUS[3]), .brpom(ADDRBUS[4]),
    .xrpom(ADDRBUS[5]), .bxpom(ADDRBUS[6]), .Adr3__0(kmadr_1_adr3__0));
  ROM16x17 rom16x17_1 (
    .A3__0(reg4_inc_ld_1_a3__0), .CS(1'b1),
    .DOUT({rom16x17_1_dout, rom16x17_1_dout_2, stEXEC, clADDR, ldMDR, rdMEM_t, mxMAR1, mxB1, mxMAR0, ldMAR, mxB0, ldB}));
  not not_2 (not_2_out, or_1_out);
  DC3_8 dc3_8_1 (
    .En(1'b1), .X2__0(rom16x17_1_dout_2), .D1(bruncnd), .D2(brnotADDR), .D3(brnotFCBUS), .D4(bradr));  // open: D0, D5, D6, D7
  or or_1 (or_1_out, bruncnd, bradr, brcnd);
  not not_3 (not_3_out, PHASEFFBUS[1]);
  not not_4 (not_4_out, in_3);
  and and_1 (and_1_out, not_3_out, brnotADDR);
  and and_2 (and_2_out, brnotFCBUS, not_4_out);
  or or_2 (brcnd, and_1_out, and_2_out);
  assign CFFBUS[3] = clADDR ? 1'b1 : 1'bz;  // Controlled_Buffer controlled_buffer_1
  assign CFFBUS[4] = stEXEC ? 1'b1 : 1'bz;  // Controlled_Buffer controlled_buffer_2
  assign CMEMBUS[0] = ldMAR ? 1'b1 : 1'bz;  // Controlled_Buffer controlled_buffer_3
  assign CMEMBUS[2] = ldMDR ? 1'b1 : 1'bz;  // Controlled_Buffer controlled_buffer_4
  assign CMEMBUS[3] = rdMEM_t ? 1'b1 : 1'bz;  // Controlled_Buffer controlled_buffer_5
  assign CMEMBUS[6] = mxMAR0 ? 1'b1 : 1'bz;  // Controlled_Buffer controlled_buffer_6
  assign CMEMBUS[7] = mxMAR1 ? 1'b1 : 1'bz;  // Controlled_Buffer controlled_buffer_7
  assign CREGBUS[2] = ldB ? 1'b1 : 1'bz;  // Controlled_Buffer controlled_buffer_8
  assign CREGBUS[3] = mxB0 ? 1'b1 : 1'bz;  // Controlled_Buffer controlled_buffer_9
  assign CREGBUS[4] = mxB1 ? 1'b1 : 1'bz;  // Controlled_Buffer controlled_buffer_10
  assign rdMEM = rdMEM_t ? 1'b1 : 1'bz;  // Controlled_Buffer controlled_buffer_11

  // Other names for the same wires on the sheet: immed = ADDRBUS[0]; memdir = ADDRBUS[1]; regdir = ADDRBUS[2];
  //   regind = ADDRBUS[3]; brpom = ADDRBUS[4]; xrpom = ADDRBUS[5]; bxpom = ADDRBUS[6]; CLK = in_2; FCBUS = in_3;
  //   HALT = INSTRUCBUS[0]; RTS = INSTRUCBUS[1]; RTI = INSTRUCBUS[2]; STBR0 = INSTRUCBUS[3]; STXR0 = INSTRUCBUS[4];
  //   STBR1 = INSTRUCBUS[5]; STXR1 = INSTRUCBUS[6]; STRCPY = INSTRUCBUS[7]; STAR = INSTRUCBUS[8];
  //   JNEQ = INSTRUCBUS[9]; JLSSU = INSTRUCBUS[10]; JLSS = INSTRUCBUS[11]; JMP = INSTRUCBUS[12]; LD = INSTRUCBUS[13];
  //   ST = INSTRUCBUS[14]; AND = INSTRUCBUS[15]; ADD = INSTRUCBUS[16]; CMP = INSTRUCBUS[17]; JSR = INSTRUCBUS[18];
  //   CLR = INSTRUCBUS[19]; FETCH = PHASEFFBUS[0]; ADDR = PHASEFFBUS[1]; EXEC = PHASEFFBUS[2]; INTR = PHASEFFBUS[3];
  //   rst = in_1

  // Notes on the sheet:
  //   Operating unit - ADDR BLOCK
  //   Control unit - ADDR BLOCK
endmodule

module EXEC (
  input  in_1,
  input  in_2,
  input  in_3,
  input  [15:0] B,
  input  [3:0] PHASEFFBUS,
  input  [19:0] INSTRUCBUS,
  input  [6:0] ADDRBUS,
  input  [15:0] PSW,
  input  in_9,
  input  [15:0] MDR,
  output [15:0] ALU,
  output [15:0] A,
  output [14:0] CMEMBUS,
  output [7:0] CFFBUS,
  output [11:0] CREGBUS,
  output [7:0] CPSW,
  output rdMEM,
  output wrMEM
);

  wire add_t, and_1_out, and_2_out, and_3_out, and_4_out, and_5_out, and_6_out, and_7_out, and_8_out, andd,
       brcnd, brISXR0, brnotbrorjmp, brnotEXEC, brnotFCBUS, bropr, brorjmp, brregdir, bruncnd, clA, clEXEC,
       clPSWSTART, cmp_t, decSP, incpointer, incSP, ldA, ldC, ldI, ldMAR, ldMDR, ldN, ldPC, ldPSWSTART, ldV,
       ldZ, mxA0, mxA1, mxMAR0, mxMAR2, mxMDR0, mxPC0, mxPC1, not_1_out, not_2_out, not_3_out, not_4_out,
       not_5_out, not_6_out, not_7_out, or_1_out, PSWC, rdMEM_t, setpointer, stINTR, wrMEM_t, wrRF, xor_1_out;
  wire [2:0] rom64x38_1_dout39__32;
  wire [5:0] kmopr_1_adr5__0, mp2_6b_1_y, reg6_inc_ld_1_a5__0, rom64x38_1_dout39__32_2;
  wire [15:0] mp4_16b_1_y;

  DC3_8 dc3_8_1 (
    .En(1'b1), .X2__0(rom64x38_1_dout39__32), .D1(bruncnd), .D2(brnotFCBUS), .D3(brISXR0), .D4(brnotEXEC),
    .D5(brregdir), .D6(brnotbrorjmp), .D7(bropr));  // open: D0
  MP4_16b mp4_16b_1 (.En(1'b1), .S0(mxA0), .S1(mxA1), .I0(ALU), .I1(B), .I2(MDR), .Y(mp4_16b_1_y));  // open: I3
  not not_1 (not_1_out, in_1);
  REG16_LD reg16_ld_1 (.I15__0(mp4_16b_1_y), .LD(ldA), .CLK(in_2), .A15__0(A), .mr(not_1_out));
  not not_2 (not_2_out, in_1);
  KMOPR kmopr_1 (
    .HALT(INSTRUCBUS[0]), .RTS(INSTRUCBUS[1]), .RTI(INSTRUCBUS[2]), .STBR0(INSTRUCBUS[3]),
    .STXR0(INSTRUCBUS[4]), .STBR1(INSTRUCBUS[5]), .STXR1(INSTRUCBUS[6]), .STRCPY(INSTRUCBUS[7]),
    .STAR(INSTRUCBUS[8]), .JNEQ(INSTRUCBUS[9]), .JLSSU(INSTRUCBUS[10]), .JLSS(INSTRUCBUS[11]),
    .JMP(INSTRUCBUS[12]), .LD(INSTRUCBUS[13]), .ST(INSTRUCBUS[14]), .AND(INSTRUCBUS[15]),
    .ADD(INSTRUCBUS[16]), .CMP(INSTRUCBUS[17]), .JSR(INSTRUCBUS[18]), .CLR(INSTRUCBUS[19]),
    .Adr5__0(kmopr_1_adr5__0));
  MP2_6b mp2_6b_1 (.En(1'b1), ._5__0(rom64x38_1_dout39__32_2), .in_3(kmopr_1_adr5__0), .S0(bropr), .Y(mp2_6b_1_y));
  REG6_INC_LD reg6_inc_ld_1 (
    .I5__0(mp2_6b_1_y), .LD(or_1_out), .INC(not_3_out), .mr(not_2_out), .CLK(in_2),
    .A5__0(reg6_inc_ld_1_a5__0));
  not not_3 (not_3_out, or_1_out);
  ROM64X38 rom64x38_1 (
    .A5__0(reg6_inc_ld_1_a5__0), .CS(1'b1),
    .DOUT39__32({rom64x38_1_dout39__32_2, rom64x38_1_dout39__32[2:1]}),
    .DOUT31__0({rom64x38_1_dout39__32[0], mxA1, mxA0, ldPSWSTART, ldI, ldMDR, clA, cmp_t, clEXEC, stINTR, mxPC0, decSP, add_t, andd, mxMDR0, ldA, incpointer, wrMEM_t, mxMAR0, setpointer, wrRF, ldC, ldV, ldZ, ldN, ldPC, mxPC1, rdMEM_t, ldMAR, mxMAR2, incSP, clPSWSTART}));
  or or_1 (or_1_out, bruncnd, brcnd, bropr);
  ALU16_ADD_SUBB_AND alu16_add_subb_and_1 (
    .Cin(1'b0), .A(A), .B(B), .add(add_t), .sub(cmp_t), .\and (andd), .F(ALU));  // open: Cout
  not not_4 (not_4_out, PHASEFFBUS[2]);
  not not_5 (not_5_out, brorjmp);
  not not_6 (not_6_out, in_3);
  and and_1 (and_1_out, not_4_out, brnotEXEC);
  and and_2 (and_2_out, ADDRBUS[2], brregdir);
  and and_3 (and_3_out, in_9, brISXR0);
  and and_4 (and_4_out, not_5_out, brnotbrorjmp);
  and and_5 (and_5_out, not_6_out, brnotFCBUS);
  not not_7 (not_7_out, PSW[3]);
  or or_2 (brcnd, and_1_out, and_2_out, and_3_out, and_4_out, and_5_out);
  xor xor_1 (xor_1_out, PSW[1], PSW[4]);
  and and_6 (and_6_out, not_7_out, INSTRUCBUS[9]);
  and and_7 (and_7_out, PSWC, INSTRUCBUS[10]);
  and and_8 (and_8_out, xor_1_out, INSTRUCBUS[11]);
  or or_3 (brorjmp, and_6_out, and_7_out, and_8_out);
  assign CPSW[0] = ldPSWSTART ? 1'b1 : 1'bz;  // Controlled_Buffer controlled_buffer_1
  assign CPSW[1] = ldV ? 1'b1 : 1'bz;  // Controlled_Buffer controlled_buffer_2
  assign CPSW[2] = ldC ? 1'b1 : 1'bz;  // Controlled_Buffer controlled_buffer_3
  assign CPSW[3] = ldZ ? 1'b1 : 1'bz;  // Controlled_Buffer controlled_buffer_4
  assign CPSW[4] = ldN ? 1'b1 : 1'bz;  // Controlled_Buffer controlled_buffer_5
  assign CPSW[6] = clPSWSTART ? 1'b1 : 1'bz;  // Controlled_Buffer controlled_buffer_6
  assign CPSW[7] = ldI ? 1'b1 : 1'bz;  // Controlled_Buffer controlled_buffer_7
  assign CMEMBUS[0] = ldMAR ? 1'b1 : 1'bz;  // Controlled_Buffer controlled_buffer_8
  assign CMEMBUS[2] = ldMDR ? 1'b1 : 1'bz;  // Controlled_Buffer controlled_buffer_9
  assign CMEMBUS[4] = ldPC ? 1'b1 : 1'bz;  // Controlled_Buffer controlled_buffer_10
  assign CMEMBUS[6] = mxMAR0 ? 1'b1 : 1'bz;  // Controlled_Buffer controlled_buffer_11
  assign CMEMBUS[8] = mxMAR2 ? 1'b1 : 1'bz;  // Controlled_Buffer controlled_buffer_12
  assign CMEMBUS[9] = mxMDR0 ? 1'b1 : 1'bz;  // Controlled_Buffer controlled_buffer_13
  assign CMEMBUS[11] = mxPC0 ? 1'b1 : 1'bz;  // Controlled_Buffer controlled_buffer_14
  assign CMEMBUS[12] = mxPC1 ? 1'b1 : 1'bz;  // Controlled_Buffer controlled_buffer_15
  assign CFFBUS[5] = clEXEC ? 1'b1 : 1'bz;  // Controlled_Buffer controlled_buffer_16
  assign CFFBUS[6] = stINTR ? 1'b1 : 1'bz;  // Controlled_Buffer controlled_buffer_17
  assign CREGBUS[5] = wrRF ? 1'b1 : 1'bz;  // Controlled_Buffer controlled_buffer_18
  assign CREGBUS[7] = incSP ? 1'b1 : 1'bz;  // Controlled_Buffer controlled_buffer_19
  assign CREGBUS[8] = decSP ? 1'b1 : 1'bz;  // Controlled_Buffer controlled_buffer_20
  assign CREGBUS[9] = setpointer ? 1'b1 : 1'bz;  // Controlled_Buffer controlled_buffer_21
  assign CREGBUS[10] = incpointer ? 1'b1 : 1'bz;  // Controlled_Buffer controlled_buffer_22
  assign rdMEM = rdMEM_t ? 1'b1 : 1'bz;  // Controlled_Buffer controlled_buffer_23
  assign wrMEM = wrMEM_t ? 1'b1 : 1'bz;  // Controlled_Buffer controlled_buffer_24

  // Other names for the same wires on the sheet: A15__0[15:0] = A; immed = ADDRBUS[0]; memdir = ADDRBUS[1];
  //   regdir = ADDRBUS[2]; regind = ADDRBUS[3]; brpom = ADDRBUS[4]; xrpom = ADDRBUS[5]; bxpom = ADDRBUS[6];
  //   ALU15__0[15:0] = ALU; B15__0[15:0] = B; CLK = in_2; FCBUS = in_3; HALT = INSTRUCBUS[0]; RTS = INSTRUCBUS[1];
  //   RTI = INSTRUCBUS[2]; STBR0 = INSTRUCBUS[3]; STXR0 = INSTRUCBUS[4]; STBR1 = INSTRUCBUS[5]; STXR1 = INSTRUCBUS[6];
  //   STRCPY = INSTRUCBUS[7]; STAR = INSTRUCBUS[8]; JNEQ = INSTRUCBUS[9]; JLSSU = INSTRUCBUS[10];
  //   JLSS = INSTRUCBUS[11]; JMP = INSTRUCBUS[12]; LD = INSTRUCBUS[13]; ST = INSTRUCBUS[14]; AND = INSTRUCBUS[15];
  //   ADD = INSTRUCBUS[16]; CMP = INSTRUCBUS[17]; JSR = INSTRUCBUS[18]; CLR = INSTRUCBUS[19]; ISXR0 = in_9;
  //   MDR15__0[15:0] = MDR; FETCH = PHASEFFBUS[0]; ADDR = PHASEFFBUS[1]; EXEC = PHASEFFBUS[2]; INTR = PHASEFFBUS[3];
  //   PSWV = PSW[1]; PSWC_t = PSW[2]; PSWZ = PSW[3]; PSWN = PSW[4]; rst = in_1

  // Notes on the sheet:
  //   Accumulator
  //   Operating unit - EXEC BLOCK
  //   Control unit - EXEC BLOCK
  //   ALU unit
  //    Scheme of branch or jump signal formation
endmodule

module INTR (
  input  in_1,
  input  in_2,
  input  in_3,
  input  [3:0] PHASEFFBUS,
  input  [19:0] INSTRUCBUS,
  input  [15:0] PSW,
  input  [7:0] intr,
  output [15:0] ADDIVTP,
  output [2:0] UEXT2__0,
  output inta,
  output [14:0] CMEMBUS,
  output [7:0] CFFBUS,
  output [11:0] CREGBUS,
  output rdMEM,
  output wrMEM
);

  wire and_2_out, and_3_out, and_4_out, brcnd, brnotFCBUS, brnotINTR, brnotprekid, bruncnd, clINTR, decSP,
       ldMAR, ldMDR, mxMAR1, mxMAR2, mxMDR0, mxMDR1, not_1_out, not_2_out, not_3_out, not_4_out, not_5_out,
       not_6_out, not_7_out, or_2_out, prekid, prper, rdMEM_t, stFETCH, wrMEM_t;
  wire [2:0] IVTDSP15__0, rom16x19_1_dout_2;
  wire [3:0] reg4_inc_ld_1_a3__0, rom16x19_1_dout;
  wire [15:0] IVTP15__0;

  and and_1 (prekid, prper, PSW[15], not_1_out);
  not not_1 (not_1_out, INSTRUCBUS[0]);
  not not_2 (not_2_out, in_1);
  REG4_INC_LD reg4_inc_ld_1 (
    .I3__0(rom16x19_1_dout), .LD(or_2_out), .INC(not_4_out), .mr(not_2_out), .CLK(in_2),
    .A3__0(reg4_inc_ld_1_a3__0));
  DC3_8 dc3_8_1 (
    .En(1'b1), .X2__0(rom16x19_1_dout_2), .D1(bruncnd), .D2(brnotINTR), .D3(brnotprekid), .D4(brnotFCBUS));  // open: D0, D5, D6, D7
  not not_3 (not_3_out, in_1);
  not not_4 (not_4_out, or_2_out);
  ROM16x19 rom16x19_1 (
    .A3__0(reg4_inc_ld_1_a3__0), .CS(1'b1),
    .DOUT({rom16x19_1_dout, rom16x19_1_dout_2, clINTR, stFETCH, rdMEM_t, mxMAR1, inta, mxMDR0, wrMEM_t, decSP, ldMDR, mxMDR1, ldMAR, mxMAR2}));
  or or_1 (prper, intr[7], intr[6], intr[5], intr[4], intr[3], intr[2], intr[1], intr[0]);
  REG16_LD reg16_ld_1 (.CLK(in_2), .A15__0(IVTP15__0), .mr(not_3_out));  // open: I15__0, LD
  or or_2 (or_2_out, bruncnd, brcnd);
  CD8 cd8_1 (
    .En(1'b1), .C7(intr[7]), .C6(intr[6]), .C5(intr[5]), .C4(intr[4]), .C3(intr[3]), .C2(intr[2]),
    .C1(intr[1]), .C0(intr[0]), .Z2(UEXT2__0[2]), .Z1(UEXT2__0[1]), .Z0(UEXT2__0[0]));  // open: W
  REG3_LD reg3_ld_1 (.I2__0(UEXT2__0), .LD(inta), .CLK(in_2), .A2__0(IVTDSP15__0));  // open: mr
  ADD16 add16_1 (.C0(1'b0), .A(IVTP15__0), .B({{13{1'b0}}, IVTDSP15__0}), .F(ADDIVTP));  // open: C16
  not not_5 (not_5_out, PHASEFFBUS[3]);
  not not_6 (not_6_out, prekid);
  not not_7 (not_7_out, in_3);
  and and_2 (and_2_out, not_5_out, brnotINTR);
  and and_3 (and_3_out, not_6_out, brnotprekid);
  and and_4 (and_4_out, not_7_out, brnotFCBUS);
  or or_3 (brcnd, and_2_out, and_3_out, and_4_out);
  assign CMEMBUS[0] = ldMAR ? 1'b1 : 1'bz;  // Controlled_Buffer controlled_buffer_1
  assign CMEMBUS[2] = ldMDR ? 1'b1 : 1'bz;  // Controlled_Buffer controlled_buffer_2
  assign CMEMBUS[7] = mxMAR1 ? 1'b1 : 1'bz;  // Controlled_Buffer controlled_buffer_3
  assign CMEMBUS[8] = mxMAR2 ? 1'b1 : 1'bz;  // Controlled_Buffer controlled_buffer_4
  assign CMEMBUS[9] = mxMDR0 ? 1'b1 : 1'bz;  // Controlled_Buffer controlled_buffer_5
  assign CMEMBUS[10] = mxMDR1 ? 1'b1 : 1'bz;  // Controlled_Buffer controlled_buffer_6
  assign CFFBUS[0] = stFETCH ? 1'b1 : 1'bz;  // Controlled_Buffer controlled_buffer_7
  assign CFFBUS[7] = clINTR ? 1'b1 : 1'bz;  // Controlled_Buffer controlled_buffer_8
  assign CREGBUS[8] = decSP ? 1'b1 : 1'bz;  // Controlled_Buffer controlled_buffer_9
  assign rdMEM = rdMEM_t ? 1'b1 : 1'bz;  // Controlled_Buffer controlled_buffer_10
  assign wrMEM = wrMEM_t ? 1'b1 : 1'bz;  // Controlled_Buffer controlled_buffer_11

  // Other names for the same wires on the sheet: ldBRU = inta; ADDIVTP15__0[15:0] = ADDIVTP; CLK = in_2; FCBUS = in_3;
  //   HALT = INSTRUCBUS[0]; intr7__0[7:0] = intr; INTR_t = PHASEFFBUS[3]; PSWI = PSW[15]; rst = in_1

  // Notes on the sheet:
  //   Operating unit - INTR BLOCK
  //   Control unit - INTR BLOCK
  //   IVTP register
endmodule

module RAM (
  input  [15:0] in_1,
  input  in_2,
  input  [15:0] in_3,
  input  in_4,
  input  in_5,
  input  in_6,
  output [15:0] out_7,
  output out_8
);

  wire and_1_out, and_2_out, CNT0, LDCNT, not_1_out, not_2_out, not_3_out, notCNT0, or_1_out, rsff_2_q, sl,
       xor_1_out;
  wire [3:0] CNT, LFSR;

  RSFF rsff_1 (.S(in_6), .CLK(in_2), .R(1'b0), .Q(sl));  // open: Sd, Rd, notQ
  or or_1 (or_1_out, in_4, in_5);
  REG4_LD_SL_SR reg4_ld_sl_sr_1 (
    .I3__0(4'b1111), .LD(in_6), .IR(1'b0), .SR(1'b0), .IL(xor_1_out), .SL(sl), .CLK(in_2), .A3__0(LFSR));  // open: mr
  RisingEdge risingedge_1 (.INPUT(or_1_out), .CLK(in_2), .OUTPUT(LDCNT));
  MEM_64Kx16 mem_64kx16_1 (.WR_RD(in_4), .A15__0(in_1), .DIN(in_3), .CS(1'b1), .CLK(in_2), .DOUT(out_7));
  xor xor_1 (xor_1_out, LFSR[2], LFSR[3]);
  and and_1 (and_1_out, CNT0, not_1_out);
  not not_1 (not_1_out, LDCNT);
  RSFF rsff_2 (.S(LDCNT), .CLK(in_2), .R(and_1_out), .Rd(not_2_out), .Q(rsff_2_q));  // open: Sd, notQ
  not not_2 (not_2_out, in_6);
  and and_2 (and_2_out, rsff_2_q, CNT0);
  REG4m_DEC_LD reg4m_dec_ld_1 (
    .I3__0(LFSR), .LD(LDCNT), .Ein(notCNT0), .DEC(notCNT0), .CLK(in_2), .A3__0(CNT));  // open: Eout, mr
  or or_2 (notCNT0, CNT[0], CNT[1], CNT[2], CNT[3]);
  RSFF rsff_3 (.S(and_2_out), .CLK(in_2), .R(out_8), .Rd(not_3_out), .Q(out_8));  // open: Sd, notQ
  not not_3 (not_3_out, in_6);
  not not_4 (CNT0, notCNT0);

  // Other names for the same wires on the sheet: ADR[15:0] = in_1; CLK = in_2; DIN[15:0] = in_3; DOUT[15:0] = out_7;
  //   fc = out_8; RDMEM = in_5; rst = in_6; WRMEM = in_4

  // Notes on the sheet:
  //   Random number represents the memory access time
  //   Counter to generate a random number
  //   Unit for generating function complete (fc) signals
  //   Random number decrement counter
endmodule
